// Logisim project Task1.3.circ as structural Verilog: 1 circuit, main circuit main
// Z2
module main (
  input  X1,
  input  X2,
  input  X3,
  input  X4,
  output Z1,
  output Z2
);

  wire _1_2_out, _1_out, _2_2_out, _2_out, _3_2_out, _3_out, _4_2_out, _4_out, _5_2_out, _5_out, not_1_out,
       not_2_out, not_3_out, not_4_out;

  not not_1 (not_1_out, X1);
  not not_2 (not_2_out, X2);
  not not_3 (not_3_out, X3);
  not not_4 (not_4_out, X4);
  and _1 (_1_out, not_1_out, not_2_out, not_4_out);
  and _2 (_2_out, X3, not_4_out);
  and _3 (_3_out, not_1_out, X2, X4);
  and _4 (_4_out, X1, not_2_out, X4);
  and _5 (_5_out, not_1_out, X3);
  and _1_2 (_1_2_out, not_1_out, not_3_out, not_4_out);
  and _2_2 (_2_2_out, not_1_out, not_2_out, not_3_out);
  and _3_2 (_3_2_out, X1, not_2_out, not_3_out);
  and _4_2 (_4_2_out, X1, not_3_out, X4);
  and _5_2 (_5_2_out, X1, X2, X3);
  or or_1 (Z1, _1_out, _2_out, _3_out, _4_out, _5_out);
  or or_2 (Z2, _1_2_out, _2_2_out, _3_2_out, _4_2_out, _5_2_out);
endmodule
