// Logisim project fullAdder4Bits.circ as structural Verilog: 1 circuit, main circuit main
module main (
  input  A4,
  input  B4,
  input  A3,
  input  B3,
  input  A2,
  input  B2,
  input  A1,
  input  B1,
  input  C_in,
  output C3,
  output C2,
  output C1,
  output C4,
  output R4,
  output R3,
  output R2,
  output out_17
);

  wire and_1_out, and_2_out, and_3_out, and_4_out, and_5_out, and_6_out, and_7_out, and_8_out, xor_1_out,
       xor_3_out, xor_5_out, xor_7_out;

  or or_1 (C4, and_1_out, and_2_out);
  and and_1 (and_1_out, A4, B4);
  and and_2 (and_2_out, xor_1_out, C3);
  xor xor_1 (xor_1_out, A4, B4);
  xor xor_2 (R4, xor_1_out, C3);
  or or_2 (C3, and_3_out, and_4_out);
  and and_3 (and_3_out, A3, B3);
  and and_4 (and_4_out, xor_3_out, C2);
  xor xor_3 (xor_3_out, A3, B3);
  xor xor_4 (R3, xor_3_out, C2);
  or or_3 (C2, and_5_out, and_6_out);
  and and_5 (and_5_out, A2, B2);
  and and_6 (and_6_out, xor_5_out, C1);
  xor xor_5 (xor_5_out, A2, B2);
  xor xor_6 (R2, xor_5_out, C1);
  or or_4 (C1, and_7_out, and_8_out);
  and and_7 (and_7_out, A1, B1);
  and and_8 (and_8_out, xor_7_out, C_in);
  xor xor_7 (xor_7_out, A1, B1);
  xor xor_8 (out_17, xor_7_out, C_in);
endmodule
