// Logisim project ControlLogic_template.circ as structural Verilog: 1 circuit, main circuit main
module main (
  output T5,
  output T6,
  output T7,
  output T8,
  output P0,
  output P1,
  output P2,
  output P3,
  output P4,
  output P5,
  output A0,
  output A1,
  output A2,
  output Mr,
  output Mw,
  output Cr
);

  wire and_1_out, clock_1_out, d_ff_4_q, pull_resistor_1_node;

  Clock clock_1 (.out(clock_1_out));
  nor nor_1 (T5, T8, T7, T6);
  D_Flip_Flop d_ff_1 (.D(T5), .clk(clock_1_out), .Q(T6), .reset(and_1_out));  // open: Qn, preset
  D_Flip_Flop d_ff_2 (.D(T6), .clk(clock_1_out), .Q(T7), .reset(and_1_out));  // open: Qn, preset
  D_Flip_Flop d_ff_3 (.D(T7), .clk(clock_1_out), .Q(T8), .reset(and_1_out));  // open: Qn, preset
  Pull_Resistor pull_resistor_1 (.node(pull_resistor_1_node));
  buf buffer_1 (pull_resistor_1_node, Cr);
  D_Flip_Flop d_ff_4 (.D(pull_resistor_1_node), .clk(clock_1_out), .Q(d_ff_4_q));  // open: Qn, preset, reset
  and and_1 (and_1_out, d_ff_4_q, ~T5);  // AND_Gate
  D_Flip_Flop d_ff_5 ();  // open: clk, D, Q, Qn, preset, reset
  D_Flip_Flop d_ff_6 ();  // open: clk, D, Q, Qn, preset, reset
  D_Flip_Flop d_ff_7 ();  // open: clk, D, Q, Qn, preset, reset
  D_Flip_Flop d_ff_8 ();  // open: clk, D, Q, Qn, preset, reset

  // Notes on the sheet:
  //   buffer_1 drives only 1 and floats otherwise
  //   IR
endmodule
