// Logisim project add_subt.circ as structural Verilog: 2 circuits, main circuit main
module main (
  input  Negate_B,
  input  A0,
  input  B0,
  input  A1,
  input  B1,
  input  A2,
  input  B2,
  input  A3,
  input  B3,
  output out_10,
  output out_11,
  output out_12,
  output out_13,
  output out_14
);

  wire adder_1_out_5, adder_2_out_5, adder_3_out_5, xor_1_out, xor_2_out, xor_3_out, xor_4_out;

  xor xor_1 (xor_1_out, Negate_B, B0);
  xor xor_2 (xor_2_out, Negate_B, B1);
  xor xor_3 (xor_3_out, Negate_B, B2);
  xor xor_4 (xor_4_out, Negate_B, B3);
  Adder adder_1 (.in_2(A0), .in_3(xor_1_out), .out_4(out_10), .out_5(adder_1_out_5), .in_1(Negate_B));
  Adder adder_2 (.in_2(A1), .in_3(xor_2_out), .out_4(out_11), .out_5(adder_2_out_5), .in_1(adder_1_out_5));
  Adder adder_3 (.in_2(A2), .in_3(xor_3_out), .out_4(out_12), .out_5(adder_3_out_5), .in_1(adder_2_out_5));
  Adder adder_4 (.in_2(A3), .in_3(xor_4_out), .out_4(out_13), .out_5(out_14), .in_1(adder_3_out_5));
endmodule

module Adder (
  input  in_1,
  input  in_2,
  input  in_3,
  output out_4,
  output out_5
);

  wire and_1_out, and_2_out, xor_1_out;

  xor xor_1 (xor_1_out, in_2, in_3);
  and and_1 (and_1_out, in_2, in_3);
  xor xor_2 (out_4, in_1, xor_1_out);
  and and_2 (and_2_out, in_1, xor_1_out);
  or or_1 (out_5, and_2_out, and_1_out);
endmodule
