// Logisim project alu_ownadder.circ as structural Verilog: 4 circuits, main circuit alu
module main (
);

  alu alu_1 ();  // open: A, B, output, op_code
endmodule

module alu (
  input  [7:0] A,
  input  [7:0] B,
  input  [2:0] op_code,
  output [7:0] \output 
);

  wire [7:0] and_1_out, not_1_out, or_1_out, ripple_1_out_4;

  assign not_1_out = ~A;  // NOT_Gate not_1, 8 bits wide
  assign or_1_out = A | B;  // OR_Gate or_1, 8 bits wide
  assign and_1_out = A & B;  // AND_Gate and_1, 8 bits wide
  ripple ripple_1 (.in_1(op_code[2]), .in_2(A), .in_3(B), .out_4(ripple_1_out_4));  // open: out_5
  Multiplexer #(.select(3), .width(8), .enable("false")) multiplexer_1 (
    .in0(not_1_out), .in1(or_1_out), .in2(and_1_out), .in3(ripple_1_out_4), .in4(ripple_1_out_4),
    .out(\output ), .sel(op_code));  // open: in5, in6, in7

  // Notes on the sheet:
  //   000: not A
  //   001: A or B
  //   010: A and B
  //   011: A + B
  //   100: A - B
  //   101: -B
endmodule

module ripple (
  input  in_1,
  input  [7:0] in_2,
  input  [7:0] in_3,
  output [7:0] out_4,
  output out_5
);

  wire adder_1_out_5, adder_2_out_5, adder_3_out_5, adder_4_out_5, adder_5_out_5, adder_6_out_5,
       adder_7_out_5, xor_1_out, xor_2_out, xor_3_out, xor_4_out, xor_5_out, xor_6_out, xor_7_out, xor_8_out;

  xor xor_1 (xor_1_out, in_1, in_3[0]);
  xor xor_2 (xor_2_out, in_1, in_3[1]);
  xor xor_3 (xor_3_out, in_1, in_3[2]);
  xor xor_4 (xor_4_out, in_1, in_3[3]);
  xor xor_5 (xor_5_out, in_1, in_3[4]);
  xor xor_6 (xor_6_out, in_1, in_3[5]);
  xor xor_7 (xor_7_out, in_1, in_3[6]);
  xor xor_8 (xor_8_out, in_1, in_3[7]);
  adder adder_1 (.in_2(in_2[0]), .in_3(xor_1_out), .out_4(out_4[0]), .out_5(adder_1_out_5), .in_1(in_1));
  adder adder_2 (.in_2(in_2[1]), .in_3(xor_2_out), .out_4(out_4[1]), .out_5(adder_2_out_5), .in_1(adder_1_out_5));
  adder adder_3 (.in_2(in_2[2]), .in_3(xor_3_out), .out_4(out_4[2]), .out_5(adder_3_out_5), .in_1(adder_2_out_5));
  adder adder_4 (.in_2(in_2[3]), .in_3(xor_4_out), .out_4(out_4[3]), .out_5(adder_4_out_5), .in_1(adder_3_out_5));
  adder adder_5 (.in_2(in_2[4]), .in_3(xor_5_out), .out_4(out_4[4]), .out_5(adder_5_out_5), .in_1(adder_4_out_5));
  adder adder_6 (.in_2(in_2[5]), .in_3(xor_6_out), .out_4(out_4[5]), .out_5(adder_6_out_5), .in_1(adder_5_out_5));
  adder adder_7 (.in_2(in_2[6]), .in_3(xor_7_out), .out_4(out_4[6]), .out_5(adder_7_out_5), .in_1(adder_6_out_5));
  adder adder_8 (.in_2(in_2[7]), .in_3(xor_8_out), .out_4(out_4[7]), .out_5(out_5), .in_1(adder_7_out_5));
endmodule

module adder (
  input  in_1,
  input  in_2,
  input  in_3,
  output out_4,
  output out_5
);

  wire and_1_out, and_2_out, xor_1_out;

  xor xor_1 (xor_1_out, in_2, in_3);
  and and_1 (and_1_out, in_2, in_3);
  xor xor_2 (out_4, in_1, xor_1_out);
  and and_2 (and_2_out, in_1, xor_1_out);
  or or_1 (out_5, and_2_out, and_1_out);
endmodule
