// Logisim project ripple_carry_adder.circ as structural Verilog: 2 circuits, main circuit main
module main (
  input  A0,
  input  B0,
  input  A1,
  input  B1,
  input  A2,
  input  B2,
  input  A3,
  input  B3,
  output out_9,
  output out_10,
  output out_11,
  output out_12,
  output Carry_out
);

  wire adder_1_out_5, adder_2_out_5, adder_3_out_5;

  Adder adder_1 (.in_2(A0), .in_3(B0), .out_4(out_9), .out_5(adder_1_out_5), .in_1(1'b0));
  Adder adder_2 (.in_2(A1), .in_3(B1), .out_4(out_10), .out_5(adder_2_out_5), .in_1(adder_1_out_5));
  Adder adder_3 (.in_2(A2), .in_3(B2), .out_4(out_11), .out_5(adder_3_out_5), .in_1(adder_2_out_5));
  Adder adder_4 (.in_2(A3), .in_3(B3), .out_4(out_12), .out_5(Carry_out), .in_1(adder_3_out_5));

  // Notes on the sheet:
  //   Constant 0 carry in
endmodule

module Adder (
  input  in_1,
  input  in_2,
  input  in_3,
  output out_4,
  output out_5
);

  wire and_1_out, and_2_out, xor_1_out;

  xor xor_1 (xor_1_out, in_2, in_3);
  and and_1 (and_1_out, in_2, in_3);
  xor xor_2 (out_4, in_1, xor_1_out);
  and and_2 (and_2_out, in_1, xor_1_out);
  or or_1 (out_5, and_2_out, and_1_out);
endmodule
